# Fritzing sketch motor (saved by Fritzing 0.9.7b)

parts:
  Part1 = Arduino Mega ADK (Rev3)
  L298N1 = L298N DC motor driver
  M1 = gear-motor
  BAT1 = BC9VPC [package=bc9vpc]
  VCC1 = Battery
  M2 = gear-motor

nets:
  N1: Part1.D13_PWM, L298N1.ENB
  N2: Part1.D12_PWM, L298N1.IN4
  N3: Part1.D11_PWM, L298N1.IN3
  N4: Part1.D10_PWM, L298N1.IN2
  N5: Part1.D9_PWM, L298N1.IN1
  N6: Part1.D8_PWM, L298N1.ENA
  N7: Part1.VIN, BAT1.V+
  N8: L298N1.OUT1, M1.pin_2
  N9: L298N1.OUT2, M1.pin_1
  N10: L298N1.OUT3, M2.pin_2
  N11: L298N1.OUT4, M2.pin_1
  N12: L298N1.12V, VCC1.+
  N13: L298N1.GND, VCC1.-

custom parts:
  L298N DC motor driver: 2x DC motor driver with 78M05 positive voltage regulator (7..35 V) L298N: max 46 V, 2 A Set 5 V Enable jumper to enable 5 V regultor (needed for the L298N) and +5 V output at screw terminal or supply external +5 V at screw terminal Set ENA and/or ENB to +5 V to enable motor permanently or supply ENA and/or ENB with PWM signal IN1 and IN2 set rotation directory for motor A (OUT1/OUT2) IN2 and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
